// Logisim project alu.circ as structural Verilog: 2 circuits, main circuit alu
module alu (
  input  [31:0] A,
  input  [31:0] B,
  input  [3:0] ALUSel,
  output [31:0] Result
);

  wire [0:0] slt2;
  wire [30:0] multiplier_3_out;
  wire [31:0] add0, and7, mul8, mulh9, mulhu11, or6, sll1, sra13, srl5, sub12, xor4;
  wire [31:31] xor_2_out;

  Adder #(.width(32)) adder_1 (.a(A), .b(B), .out(add0));  // open: cin, cout
  Shifter #(.width(32)) shifter_1 (.in(A), .\dist (B[4:0]), .out(sll1));
  Comparator #(.width(32)) comparator_1 (.a(A), .b(B), .lt(slt2[0]));  // open: gt, eq
  assign xor4 = A ^ B;  // XOR_Gate xor_1, 32 bits wide
  Shifter #(.shift("lr"), .width(32)) shifter_2 (.in(A), .\dist (B[4:0]), .out(srl5));
  assign or6 = A | B;  // OR_Gate or_1, 32 bits wide
  assign and7 = A & B;  // AND_Gate and_1, 32 bits wide
  Multiplier #(.width(32)) multiplier_1 (.a(A), .b(B), .out(mul8));  // open: cin, cout
  Multiplier #(.width(32)) multiplier_2 (.a(A), .b(B), .cout(mulhu11));  // open: out, cin
  Multiplier #(.width(31)) multiplier_3 (.a(A[30:0]), .b(B[30:0]), .out(multiplier_3_out));  // open: cin, cout
  Subtractor #(.width(32)) subtractor_1 (.a(A), .b(B), .out(sub12));  // open: bin, bout
  Shifter #(.shift("ar"), .width(32)) shifter_3 (.in(A), .\dist (B[4:0]), .out(sra13));
  xor xor_2 (xor_2_out[31], A[31], B[31]);
  Multiplexer #(.enable("false"), .select(4), .width(32)) multiplexer_1 (
    .in0(add0), .in1(sll1), .in2({{31{1'b0}}, slt2[0]}), .in4(xor4), .in5(srl5), .in6(or6), .in7(and7),
    .in8(mul8), .in9(mulh9), .in11(mulhu11), .in12(sub12), .in13(sra13), .in15(B), .out(Result), .sel(ALUSel));  // open: in3, in10, in14
  mul mul_1 (.input1(A), .input2(B), .output_mulh(mulh9));

  // Other names for the same wires on the sheet: bsel15[31:0] = B

  // Notes on the sheet:
  //   INPUTS to your circuit
  //   DON'T CHANGE THE LOCATIONS OF THE INPUTS AND OUTPUTS!
  //   OUTPUT from your circuit
endmodule

module mul (
  input  [31:0] input1,
  input  [31:0] input2,
  output [31:0] output_mulh
);

  wire xor_1_out;
  wire [31:0] multiplexer_1_out, multiplexer_2_out, multiplier_1_cout, not_1_out, not_2_out, not_3_out;

  assign not_1_out = ~input1;  // NOT_Gate not_1, 32 bits wide
  assign not_2_out = ~input2;  // NOT_Gate not_2, 32 bits wide
  Multiplexer #(.enable("false"), .width(32)) multiplexer_1 (
    .in0(input1), .in1(not_1_out), .out(multiplexer_1_out), .sel(input1[31]));
  Multiplexer #(.enable("false"), .width(32)) multiplexer_2 (
    .in0(input2), .in1(not_2_out), .out(multiplexer_2_out), .sel(input2[31]));
  xor xor_1 (xor_1_out, input2[31], input1[31]);
  Multiplier #(.width(32)) multiplier_1 (
    .a(multiplexer_1_out), .b(multiplexer_2_out), .cout(multiplier_1_cout));  // open: out, cin
  Multiplexer #(.enable("false"), .width(32)) multiplexer_3 (
    .in0(multiplier_1_cout), .in1(not_3_out), .out(output_mulh), .sel(xor_1_out));
  assign not_3_out = ~multiplier_1_cout;  // NOT_Gate not_3, 32 bits wide

  // Other names for the same wires on the sheet: A[31:0] = input1; B[31:0] = input2
endmodule
