// Logisim project branch-comp.circ as structural Verilog: 1 circuit, main circuit branch_comp
module branch_comp (
  input  [31:0] rs1,
  input  [31:0] rs2,
  input  BrUn,
  output BrEq,
  output BrLt
);

  wire and_1_out, and_2_out, and_3_out, and_4_out, comparator_1_eq, comparator_1_lt, comparator_2_eq,
       comparator_2_lt, not_1_out;
  wire [32:0] bit_extender_1_out, bit_extender_2_out;

  assign bit_extender_1_out = {{1{1'b0}}, rs1};  // Bit_Extender bit_extender_1
  assign bit_extender_2_out = {{1{1'b0}}, rs2};  // Bit_Extender bit_extender_2
  Comparator #(.width(33)) comparator_1 (
    .a(bit_extender_1_out), .b(bit_extender_2_out), .eq(comparator_1_eq), .lt(comparator_1_lt));  // open: gt
  not not_1 (not_1_out, BrUn);
  Comparator #(.width(32)) comparator_2 (.a(rs1), .b(rs2), .eq(comparator_2_eq), .lt(comparator_2_lt));  // open: gt
  and and_1 (and_1_out, BrUn, comparator_1_eq);
  and and_2 (and_2_out, not_1_out, comparator_2_eq);
  and and_3 (and_3_out, BrUn, comparator_1_lt);
  and and_4 (and_4_out, not_1_out, comparator_2_lt);
  or or_1 (BrEq, and_1_out, and_2_out);
  or or_2 (BrLt, and_3_out, and_4_out);

  // Notes on the sheet:
  //   INPUTS to your circuit
  //   DON'T CHANGE THE LOCATIONS OF THE INPUTS AND OUTPUTS!
  //   OUTPUT from your circuit
endmodule
