// Logisim project control-logic.circ as structural Verilog: 1 circuit, main circuit control_logic
module control_logic (
  input  [31:0] inst,
  input  BrEq,
  input  BrLt,
  output PCSel,
  output RegWEn,
  output [2:0] ImmSel,
  output BrUn,
  output ASel,
  output BSel,
  output [3:0] ALUSel,
  output MemRW,
  output [1:0] WBSel,
  output CSRSel,
  output CSRWen
);

  wire and_1_out, and_2_out, and_3_out, and_4_out, and_5_out, and_6_out, and_7_out, and_20_out, and_21_out,
       comparator_1_eq, comparator_2_eq, comparator_3_eq, comparator_4_eq, comparator_5_eq, comparator_6_eq,
       comparator_7_eq, comparator_8_eq, comparator_9_eq, comparator_10_eq, comparator_11_eq,
       comparator_12_eq, comparator_13_eq, comparator_14_eq, comparator_15_eq, comparator_16_eq,
       comparator_17_eq, comparator_18_eq, comparator_19_eq, comparator_20_eq, comparator_21_eq,
       comparator_22_eq, comparator_23_eq, comparator_24_eq, comparator_25_eq, comparator_26_eq,
       comparator_27_eq, comparator_28_eq, comparator_29_eq, is_AUIPC, is_B, is_CSR, is_IA, is_IL, is_JAL,
       is_JALR, IS_O, is_R, is_S, multiplexer_2_out, not_1_out, not_2_out, not_3_out, not_5_out, not_16_out,
       not_17_out, or_2_out, or_6_out, or_7_out, or_8_out, or_10_out;
  wire [1:0] ALU_MUX;
  wire [2:0] and_22_out, and_23_out, and_24_out, and_25_out, and_28_out, and_29_out, and_30_out;
  wire [2:2] and_26_out, or_11_out, or_12_out;
  wire [3:0] ALU_I, ALU_R;
  wire [3:3] ALU_LUI, ALU_O;
  wire [6:0] not_6_out, not_7_out, not_8_out, not_9_out, not_10_out, not_11_out, not_12_out, not_13_out,
       not_14_out, not_15_out, xor_1_out, xor_2_out, xor_3_out, xor_4_out, xor_5_out, xor_6_out, xor_7_out,
       xor_8_out, xor_9_out, xor_10_out;

  not not_1 (not_1_out, BrEq);
  not not_2 (not_2_out, BrLt);
  Comparator #(.width(3)) comparator_1 (.a(3'b000), .b(inst[14:12]), .eq(comparator_1_eq));  // open: gt, lt
  and and_1 (and_1_out, comparator_1_eq, BrEq);
  Comparator #(.width(3)) comparator_2 (.a(inst[14:12]), .b(3'b001), .eq(comparator_2_eq));  // open: gt, lt
  and and_2 (and_2_out, comparator_2_eq, not_1_out);
  Comparator #(.width(3)) comparator_3 (.a(inst[14:12]), .b(3'b100), .eq(comparator_3_eq));  // open: gt, lt
  and and_3 (and_3_out, comparator_3_eq, BrLt);
  Comparator #(.width(3)) comparator_4 (.a(inst[14:12]), .b(3'b101), .eq(comparator_4_eq));  // open: gt, lt
  and and_4 (and_4_out, comparator_4_eq, not_2_out);
  Comparator #(.width(3)) comparator_5 (.a(inst[14:12]), .b(3'b110), .eq(comparator_5_eq));  // open: gt, lt
  and and_5 (and_5_out, comparator_5_eq, BrLt);
  Comparator #(.width(3)) comparator_6 (.a(inst[14:12]), .b(3'b111), .eq(comparator_6_eq));  // open: gt, lt
  and and_6 (and_6_out, comparator_6_eq, not_3_out);
  not not_3 (not_3_out, BrLt);
  or or_1 (IS_O, is_IL, is_JALR, is_JAL, is_S, is_B, is_AUIPC);
  not not_4 (ALU_O[3], IS_O);
  Comparator #(.width(10)) comparator_7 (
    .a({10{1'b0}}), .b({inst[14:12], inst[31:25]}), .eq(comparator_7_eq));  // open: gt, lt
  Comparator #(.width(10)) comparator_8 (
    .a(10'h80), .b({inst[14:12], inst[31:25]}), .eq(comparator_8_eq));  // open: gt, lt
  Comparator #(.width(10)) comparator_9 (
    .a(10'h100), .b({inst[14:12], inst[31:25]}), .eq(comparator_9_eq));  // open: gt, lt
  Comparator #(.width(10)) comparator_10 (
    .a(10'h200), .b({inst[14:12], inst[31:25]}), .eq(comparator_10_eq));  // open: gt, lt
  Comparator #(.width(10)) comparator_11 (
    .a(10'h280), .b({inst[14:12], inst[31:25]}), .eq(comparator_11_eq));  // open: gt, lt
  Comparator #(.width(10)) comparator_12 (
    .a(10'h300), .b({inst[14:12], inst[31:25]}), .eq(comparator_12_eq));  // open: gt, lt
  Comparator #(.width(10)) comparator_13 (
    .a(10'h380), .b({inst[14:12], inst[31:25]}), .eq(comparator_13_eq));  // open: gt, lt
  Comparator #(.width(10)) comparator_14 (
    .a(10'h1), .b({inst[14:12], inst[31:25]}), .eq(comparator_14_eq));  // open: gt, lt
  Comparator #(.width(10)) comparator_15 (
    .a(10'h81), .b({inst[14:12], inst[31:25]}), .eq(comparator_15_eq));  // open: gt, lt
  Comparator #(.width(10)) comparator_16 (
    .a(10'h181), .b({inst[14:12], inst[31:25]}), .eq(comparator_16_eq));  // open: gt, lt
  Comparator #(.width(10)) comparator_17 (
    .a(10'h20), .b({inst[14:12], inst[31:25]}), .eq(comparator_17_eq));  // open: gt, lt
  Comparator #(.width(10)) comparator_18 (
    .a(10'h2a0), .b({inst[14:12], inst[31:25]}), .eq(comparator_18_eq));  // open: gt, lt
  Comparator #(.width(10)) comparator_19 (
    .a(10'h280), .b({inst[14:12], inst[31:25]}), .eq(comparator_19_eq));  // open: gt, lt
  Comparator #(.width(3)) comparator_20 (.a(3'b000), .b(inst[14:12]), .eq(comparator_20_eq));  // open: gt, lt
  Comparator #(.width(3)) comparator_21 (.a(3'b001), .b(inst[14:12]), .eq(comparator_21_eq));  // open: gt, lt
  Comparator #(.width(3)) comparator_22 (.a(3'b010), .b(inst[14:12]), .eq(comparator_22_eq));  // open: gt, lt
  Comparator #(.width(3)) comparator_23 (.a(3'b100), .b(inst[14:12]), .eq(comparator_23_eq));  // open: gt, lt
  Comparator #(.width(3)) comparator_24 (.a(3'b110), .b(inst[14:12]), .eq(comparator_24_eq));  // open: gt, lt
  Comparator #(.width(3)) comparator_25 (.a(3'b111), .b(inst[14:12]), .eq(comparator_25_eq));  // open: gt, lt
  or or_2 (or_2_out, and_1_out, and_2_out, and_3_out, and_4_out, and_5_out, and_6_out);
  or or_3 (RegWEn, is_R, is_IA, is_JALR, is_IL, is_JAL, ALU_LUI[3], is_AUIPC);
  and and_7 (and_7_out, is_B, or_2_out);
  or or_4 (PCSel, is_JALR, is_JAL, and_7_out);
  Priority_Encoder #(.select(4)) priority_encoder_1 (
    .in0(comparator_7_eq), .in1(comparator_8_eq), .in2(comparator_9_eq), .in4(comparator_10_eq),
    .in5(comparator_11_eq), .in6(comparator_12_eq), .in7(comparator_13_eq), .in8(comparator_14_eq),
    .in9(comparator_15_eq), .in11(comparator_16_eq), .in12(comparator_17_eq), .in13(comparator_18_eq),
    .out(ALU_R), .en_in(is_R));  // open: in3, in10, in14, in15, gs, en_out
  Priority_Encoder #(.select(4)) priority_encoder_2 (
    .in0(comparator_20_eq), .in1(comparator_21_eq), .in2(comparator_22_eq), .in4(comparator_23_eq),
    .in5(comparator_19_eq), .in6(comparator_24_eq), .in7(comparator_25_eq), .in13(comparator_18_eq),
    .out(ALU_I), .en_in(is_IA));  // open: in3, in8, in9, in10, in11, in12, in14, in15, gs, en_out
  Multiplexer #(.enable("false"), .select(2), .width(4)) multiplexer_1 (
    .in0(ALU_R), .in1(ALU_I), .in2({4{ALU_LUI[3]}}), .in3({4{ALU_O[3]}}), .out(ALUSel), .sel(ALU_MUX));
  or or_5 (ASel, is_B, is_JAL, is_AUIPC);
  or or_6 (or_6_out, is_JAL, is_JALR);
  Multiplexer #(.enable("false"), .select(3)) multiplexer_2 (
    .in0(1'b0), .in1(1'b0), .in2(1'b0), .in3(1'b0), .in4(1'b0), .in5(1'b0), .in6(1'b1), .in7(1'b1),
    .out(multiplexer_2_out), .sel(inst[14:12]));
  or or_7 (or_7_out, is_IA, is_R, ALU_LUI[3], is_AUIPC);
  Priority_Encoder #(.select(2)) priority_encoder_3 (
    .in0(is_IL), .in1(or_7_out), .in2(or_6_out), .out(WBSel));  // open: in3, gs, en_out, en_in
  Priority_Encoder #(.select(2)) priority_encoder_4 (
    .in0(is_R), .in1(is_IA), .in2(ALU_LUI[3]), .in3(IS_O), .out(ALU_MUX));  // open: gs, en_out, en_in
  and and_8 (BrUn, is_B, multiplexer_2_out);
  Comparator #(.width(3)) comparator_26 (.a(3'b001), .b(inst[14:12]), .eq(comparator_26_eq));  // open: gt, lt
  Comparator #(.width(3)) comparator_27 (.a(inst[14:12]), .b(3'b101), .eq(comparator_27_eq));  // open: gt, lt
  Comparator #(.width(3)) comparator_28 (.a(3'b001), .b(inst[14:12]), .eq(comparator_28_eq));  // open: gt, lt
  Comparator #(.width(3)) comparator_29 (.a(inst[14:12]), .b(3'b101), .eq(comparator_29_eq));  // open: gt, lt
  Priority_Encoder #(.select(1)) priority_encoder_5 (
    .in0(comparator_26_eq), .in1(comparator_27_eq), .out(CSRSel), .en_in(is_CSR));  // open: gs, en_out
  or or_8 (or_8_out, comparator_28_eq, comparator_29_eq);
  and and_9 (CSRWen, is_CSR, or_8_out);
  assign xor_1_out = 7'b0110011 ^ inst[6:0];  // XOR_Gate xor_1, 7 bits wide
  assign xor_2_out = 7'b0010011 ^ inst[6:0];  // XOR_Gate xor_2, 7 bits wide
  assign xor_3_out = 7'b0000011 ^ inst[6:0];  // XOR_Gate xor_3, 7 bits wide
  assign xor_4_out = 7'b0100011 ^ inst[6:0];  // XOR_Gate xor_4, 7 bits wide
  assign xor_5_out = 7'b1100011 ^ inst[6:0];  // XOR_Gate xor_5, 7 bits wide
  assign xor_6_out = 7'b1101111 ^ inst[6:0];  // XOR_Gate xor_6, 7 bits wide
  assign xor_7_out = 7'b1100111 ^ inst[6:0];  // XOR_Gate xor_7, 7 bits wide
  assign xor_8_out = 7'b0110111 ^ inst[6:0];  // XOR_Gate xor_8, 7 bits wide
  assign xor_9_out = 7'b0010111 ^ inst[6:0];  // XOR_Gate xor_9, 7 bits wide
  assign xor_10_out = 7'b1110011 ^ inst[6:0];  // XOR_Gate xor_10, 7 bits wide
  not not_5 (not_5_out, BrEq);
  assign not_6_out = ~xor_1_out;  // NOT_Gate not_6, 7 bits wide
  assign not_7_out = ~xor_2_out;  // NOT_Gate not_7, 7 bits wide
  assign not_8_out = ~xor_3_out;  // NOT_Gate not_8, 7 bits wide
  assign not_9_out = ~xor_4_out;  // NOT_Gate not_9, 7 bits wide
  assign not_10_out = ~xor_5_out;  // NOT_Gate not_10, 7 bits wide
  assign not_11_out = ~xor_6_out;  // NOT_Gate not_11, 7 bits wide
  assign not_12_out = ~xor_7_out;  // NOT_Gate not_12, 7 bits wide
  assign not_13_out = ~xor_8_out;  // NOT_Gate not_13, 7 bits wide
  assign not_14_out = ~xor_9_out;  // NOT_Gate not_14, 7 bits wide
  assign not_15_out = ~xor_10_out;  // NOT_Gate not_15, 7 bits wide
  not not_16 (not_16_out, inst[12]);
  not not_17 (not_17_out, inst[14]);
  and and_10 (is_R, not_6_out[0], not_6_out[1], not_6_out[2], not_6_out[3], not_6_out[4], not_6_out[5], not_6_out[6]);
  and and_11 (is_IA, not_7_out[0], not_7_out[1], not_7_out[2], not_7_out[3], not_7_out[4], not_7_out[5], not_7_out[6]);
  and and_12 (is_IL, not_8_out[0], not_8_out[1], not_8_out[2], not_8_out[3], not_8_out[4], not_8_out[5], not_8_out[6]);
  and and_13 (is_S, not_9_out[0], not_9_out[1], not_9_out[2], not_9_out[3], not_9_out[4], not_9_out[5], not_9_out[6]);
  and and_14 (is_B, not_10_out[0], not_10_out[1], not_10_out[2], not_10_out[3], not_10_out[4], not_10_out[5], not_10_out[6]);
  and and_15 (is_JAL, not_11_out[0], not_11_out[1], not_11_out[2], not_11_out[3], not_11_out[4], not_11_out[5], not_11_out[6]);
  and and_16 (is_JALR, not_12_out[0], not_12_out[1], not_12_out[2], not_12_out[3], not_12_out[4], not_12_out[5], not_12_out[6]);
  and and_17 (ALU_LUI[3], not_13_out[0], not_13_out[1], not_13_out[2], not_13_out[3], not_13_out[4], not_13_out[5], not_13_out[6]);
  and and_18 (is_AUIPC, not_14_out[0], not_14_out[1], not_14_out[2], not_14_out[3], not_14_out[4], not_14_out[5], not_14_out[6]);
  and and_19 (is_CSR, not_15_out[0], not_15_out[1], not_15_out[2], not_15_out[3], not_15_out[4], not_15_out[5], not_15_out[6]);
  and and_20 (and_20_out, not_16_out, inst[13], not_17_out);
  and and_21 (and_21_out, inst[12], inst[13], inst[14], not_5_out, BrLt);
  or or_9 (BSel, is_IA, is_IL, is_S, is_B, is_JAL, is_JALR, ALU_LUI[3], is_AUIPC, is_CSR);
  or or_10 (or_10_out, and_20_out, and_21_out);
  assign and_22_out = {3{is_R}} & 3'b001;  // AND_Gate and_22, 3 bits wide
  or or_11 (or_11_out[2], is_IA, is_JALR, is_IL);
  assign and_23_out = {3{is_S}} & 3'b011;  // AND_Gate and_23, 3 bits wide
  assign and_24_out = {3{is_B}} & 3'b100;  // AND_Gate and_24, 3 bits wide
  assign and_25_out = {3{is_JAL}} & 3'b101;  // AND_Gate and_25, 3 bits wide
  or or_12 (or_12_out[2], ALU_LUI[3], is_AUIPC);
  and and_26 (and_26_out[2], CSRSel, is_CSR);
  and and_27 (MemRW, is_S, or_10_out);
  assign and_28_out = {3{or_12_out[2]}} & 3'b110;  // AND_Gate and_28, 3 bits wide
  assign and_29_out = {3{and_26_out[2]}} & 3'b111;  // AND_Gate and_29, 3 bits wide
  assign and_30_out = {3{or_11_out[2]}} & 3'b010;  // AND_Gate and_30, 3 bits wide
  assign ImmSel = and_22_out | and_30_out | and_23_out | and_29_out | and_24_out | and_25_out | and_28_out;  // OR_Gate or_13, 3 bits wide

  // Other names for the same wires on the sheet: ALU_LUI[2:0] = {3{ALU_LUI[3]}}; is_LUI = ALU_LUI[3];
  //   ALU_O[2:0] = {3{ALU_O[3]}}; funct3[2:0] = inst[14:12]; f7_imm[6:0] = inst[31:25]

  // Notes on the sheet:
  //   INPUTS to your circuit
  //   RegWen
  //   PCSel
  //   DON'T CHANGE THE LOCATIONS OF THE INPUTS AND OUTPUTS!
  //   OUTPUT from your circuit
  //   ASel
  //   BrUn
  //   WBSel
  //   BSelect
endmodule
