// Logisim project cpu.circ as structural Verilog: 1 circuit, main circuit cpu
module cpu (
  input  clk,
  input  [31:0] INSTRUCTION,
  input  [31:0] READ_DATA,
  output [31:0] WRITE_ADDRESS,
  output [31:0] PROGRAM_COUNTER,
  output [31:0] ra,
  output [31:0] sp,
  output [31:0] t0,
  output [31:0] t1,
  output [31:0] t2,
  output [31:0] s0,
  output [31:0] s1,
  output [31:0] a0,
  output [31:0] tohost,
  output [3:0] WRITE_ENABLE,
  output [31:0] WRITE_DATA
);

  wire ASel, BrEq, BrLt, BrUn, BSel, CSRSel, CSRWen, MemRW, RegWEn;
  wire [1:0] PCSel, WBSel;
  wire [2:0] ImmSel;
  wire [3:0] ALUSel, multiplexer_6_out, multiplexer_9_out, multiplexer_10_out;
  wire [4:0] bit_extender_3_out, WB_shift;
  wire [31:0] adder_2_out, adder_3_out, bit_extender_1_out, bit_extender_2_out, bit_extender_4_out,
       bit_extender_5_out, Imm, Inst, multiplexer_4_out, multiplexer_7_out, multiplexer_8_out,
       multiplexer_12_out, PC, PC_In, PC_plus_4, register_1_q, register_2_q, rs1_data, rs2_data,
       shifter_1_out, shifter_2_out, shifter_3_out, shifter_4_out, WB_Data;

  Register #(.width(32)) u_PC (.D(PC_In), .en(1'b1), .clk(clk), .Q(PROGRAM_COUNTER));  // open: clr
  Multiplexer #(.enable("false"), .select(2), .width(32)) multiplexer_1 (
    .in0(INSTRUCTION), .in1(32'h13), .in2(32'h13), .in3(32'h13), .sel(PCSel));  // open: out
  Register #(.width(32)) register_1 (.D(PROGRAM_COUNTER), .en(1'b1), .clk(clk), .Q(register_1_q));  // open: clr
  Register #(.width(32)) register_2 (.D(INSTRUCTION), .en(1'b1), .clk(clk), .Q(register_2_q));  // open: clr
  Adder #(.width(32)) adder_1 (.a(PROGRAM_COUNTER), .b(32'h4), .out(PC_plus_4));  // open: cin, cout
  Multiplexer #(.enable("false"), .width(32)) multiplexer_2 (
    .in0(PROGRAM_COUNTER), .in1(register_1_q), .out(PC), .sel(1'b1));
  Multiplexer #(.enable("false"), .width(32)) multiplexer_3 (
    .in0(INSTRUCTION), .in1(register_2_q), .out(Inst), .sel(1'b1));
  Adder #(.width(32)) adder_2 (.a(PC), .b(Imm), .out(adder_2_out));  // open: cin, cout
  Adder #(.width(32)) adder_3 (.a(rs1_data), .b(Imm), .out(adder_3_out));  // open: cin, cout
  Multiplexer #(.enable("false"), .width(32)) multiplexer_4 (
    .in0(rs1_data), .in1(Imm), .out(multiplexer_4_out), .sel(CSRSel));
  Multiplexer #(.enable("false"), .select(2), .width(32)) multiplexer_5 (
    .in0(PC_plus_4), .in1(adder_2_out), .in2(adder_3_out), .out(PC_In));  // open: in3, sel
  regfile regfile_1 (
    .rs1(INSTRUCTION[19:15]), .rs2(INSTRUCTION[24:20]), .rd(INSTRUCTION[11:7]), .Write_Data(WB_Data),
    .RegWEn(RegWEn), .clk(clk), .ra(ra), .sp(sp), .t0(t0), .t1(t1), .t2(t2), .s0(s0), .s1(s1), .a0(a0),
    .Read_Data_1(rs1_data), .Read_Data_2(rs2_data));
  branch_comp branch_comp_1 (.rs1(rs1_data), .rs2(rs2_data), .BrUn(BrUn), .BrEq(BrEq), .BrLt(BrLt));
  imm_gen imm_gen_1 (.inst(Inst), .ImmSel(ImmSel), .imm(Imm));
  // csr csr_1: pin names not known; wires that end beside it: INSTRUCTION[31:20], multiplexer_4_out, CSRWen, clk, tohost
  Multiplexer #(.enable("false"), .select(2), .width(4)) multiplexer_6 (
    .in0(4'b0001), .in1(4'b0010), .in2(4'b0100), .in3(4'b1000), .out(multiplexer_6_out),
    .sel(WRITE_ADDRESS[1:0]));
  Multiplexer #(.enable("false"), .width(32)) multiplexer_7 (
    .in0(rs1_data), .in1(PROGRAM_COUNTER), .out(multiplexer_7_out), .sel(ASel));
  Multiplexer #(.enable("false"), .width(32)) multiplexer_8 (
    .in0(rs2_data), .in1(Imm), .out(multiplexer_8_out), .sel(BSel));
  Multiplexer #(.enable("false"), .select(2), .width(4)) multiplexer_9 (
    .in0(4'b0011), .in1(4'b0110), .in2(4'b1100), .in3(4'b0000), .out(multiplexer_9_out),
    .sel(WRITE_ADDRESS[1:0]));
  alu alu_1 (.Result(WRITE_ADDRESS), .A(multiplexer_7_out), .B(multiplexer_8_out), .ALUSel(ALUSel));
  Multiplexer #(.enable("false"), .select(3), .width(4)) multiplexer_10 (
    .in0(multiplexer_9_out), .in1(multiplexer_6_out), .in2(4'b1111), .out(multiplexer_10_out),
    .sel(INSTRUCTION[14:12]));  // open: in3, in4, in5, in6, in7
  Multiplexer #(.enable("false"), .width(4)) multiplexer_11 (
    .in0(4'b0000), .in1(multiplexer_10_out), .out(WRITE_ENABLE), .sel(MemRW));
  Shifter #(.shift("lr"), .width(32)) shifter_1 (.in(READ_DATA), .\dist (WB_shift), .out(shifter_1_out));
  Shifter #(.shift("lr"), .width(32)) shifter_2 (.in(READ_DATA), .\dist (WB_shift), .out(shifter_2_out));
  control_logic control_logic_1 (
    .CSRWen(CSRWen), .PCSel(PCSel[0]), .RegWEn(RegWEn), .ImmSel(ImmSel), .BrUn(BrUn), .ASel(ASel),
    .BSel(BSel), .ALUSel(ALUSel), .MemRW(MemRW), .WBSel(WBSel), .CSRSel(CSRSel), .inst(Inst), .BrEq(BrEq),
    .BrLt(BrLt));
  assign bit_extender_1_out = {{24{shifter_1_out[7]}}, shifter_1_out[7:0]};  // Bit_Extender bit_extender_1
  assign bit_extender_2_out = {{16{shifter_2_out[15]}}, shifter_2_out[15:0]};  // Bit_Extender bit_extender_2
  Multiplexer #(.enable("false"), .select(3), .width(32)) multiplexer_12 (
    .in0(bit_extender_1_out), .in1(bit_extender_2_out), .in2(READ_DATA), .out(multiplexer_12_out),
    .sel(INSTRUCTION[14:12]));  // open: in3, in4, in5, in6, in7
  Multiplexer #(.enable("false"), .select(2), .width(32)) multiplexer_13 (
    .in0(WRITE_ADDRESS), .in1(multiplexer_12_out), .in2(tohost), .out(WB_Data), .sel(WBSel));  // open: in3
  assign bit_extender_3_out = {{3{1'b0}}, WRITE_ADDRESS[1:0]};  // Bit_Extender bit_extender_3
  assign bit_extender_4_out = {{24{1'b0}}, rs2_data[7:0]};  // Bit_Extender bit_extender_4
  assign bit_extender_5_out = {{16{1'b0}}, rs2_data[15:0]};  // Bit_Extender bit_extender_5
  Multiplier #(.width(5)) multiplier_1 (.a(bit_extender_3_out), .b(5'b01000), .out(WB_shift));  // open: cin, cout
  Shifter #(.width(32)) shifter_3 (.in(bit_extender_5_out), .\dist (WB_shift), .out(shifter_3_out));
  Shifter #(.width(32)) shifter_4 (.in(bit_extender_4_out), .\dist (WB_shift), .out(shifter_4_out));
  Multiplexer #(.enable("false"), .select(3), .width(32)) multiplexer_14 (
    .in0(shifter_3_out), .in1(shifter_4_out), .in2(rs2_data), .out(WRITE_DATA), .sel(INSTRUCTION[14:12]));  // open: in3, in4, in5, in6, in7
  // Pins of 1 and 2 bits meet at PCSel

  // Other names for the same wires on the sheet: ALU_out[31:0] = WRITE_ADDRESS; MEM_addr[1:0] = WRITE_ADDRESS[1:0];
  //   rd[4:0] = INSTRUCTION[11:7]; funct3[2:0] = INSTRUCTION[14:12]; rs1[4:0] = INSTRUCTION[19:15];
  //   CSR_address[11:0] = INSTRUCTION[31:20]; rs2[4:0] = INSTRUCTION[24:20]

  // Notes on the sheet:
  //   Pipeline
  //   Output to IMEM
  //   IMEM (do **NOT** move this)
  //   Inputs from IMEM
  //   Inputs/Outputs for testing. Do **NOT** move these.
  //   Outputs To DMEM
  //   DMEM (do **NOT** move this)
  //   Inputs From DMEM
endmodule
